// Logisim project mapa.circ as structural Verilog: 8 circuits, main circuit main
module main (
  input  [3:0] Entrada
);

  wire \Lógica_segmento_a_out_2 , \Lógica_segmento_b_out_2 , \Lógica_segmento_c_out_2 ,
       \Lógica_segmento_d_out_2 , \Lógica_segmento_e_out_2 , \Lógica_segmento_f_out_2 ,
       \Lógica_segmento_g_out_2 ;

  Logica_seg_1 \Lógica_segmento_a  (.out_2(\Lógica_segmento_a_out_2 ), .Entrada(Entrada));
  Logica_seg_2 \Lógica_segmento_b  (.out_2(\Lógica_segmento_b_out_2 ), .Entrada(Entrada));
  Logica_seg_3 \Lógica_segmento_c  (.out_2(\Lógica_segmento_c_out_2 ), .Entrada(Entrada));
  Logica_seg_4 \Lógica_segmento_d  (.out_2(\Lógica_segmento_d_out_2 ), .Entrada(Entrada));
  Logica_seg_5 \Lógica_segmento_e  (.out_2(\Lógica_segmento_e_out_2 ), .Entrada(Entrada));
  Logica_seg_6 \Lógica_segmento_f  (.out_2(\Lógica_segmento_f_out_2 ), .Entrada(Entrada));
  Logica_seg_7 \Lógica_segmento_g  (.out_2(\Lógica_segmento_g_out_2 ), .Entrada(Entrada));
  _7_Segment_Display u_7_segment_display_1 (
    .g(\Lógica_segmento_g_out_2 ), .f(\Lógica_segmento_f_out_2 ), .a(\Lógica_segmento_a_out_2 ),
    .b(\Lógica_segmento_b_out_2 ), .e(\Lógica_segmento_e_out_2 ), .d(\Lógica_segmento_d_out_2 ),
    .c(\Lógica_segmento_c_out_2 ));  // open: dp
endmodule

module Logica_seg_1 (
  input  [3:0] Entrada,
  output out_2
);

  wire and_1_out, and_2_out, and_3_out, and_4_out, and_5_out;

  and and_1 (and_1_out, Entrada[3], ~Entrada[1]);  // AND_Gate
  and and_2 (and_2_out, Entrada[1], ~Entrada[0]);  // AND_Gate
  and and_3 (and_3_out, Entrada[3], Entrada[2]);
  and and_4 (and_4_out, Entrada[2], ~Entrada[1], ~Entrada[0]);  // AND_Gate
  and and_5 (and_5_out, ~Entrada[3], ~Entrada[2], Entrada[1]);  // AND_Gate
  or or_1 (out_2, and_1_out, and_2_out, and_3_out, and_4_out, and_5_out);
endmodule

module Logica_seg_2 (
  input  [3:0] Entrada,
  output out_2
);

  wire and_1_out, and_2_out, and_3_out, and_4_out, and_5_out, and_6_out;

  and and_1 (and_1_out, ~Entrada[3], ~Entrada[2], ~Entrada[0]);  // AND_Gate
  and and_2 (and_2_out, ~Entrada[3], Entrada[2], ~Entrada[1]);  // AND_Gate
  and and_3 (and_3_out, Entrada[2], Entrada[1], Entrada[0]);
  and and_4 (and_4_out, Entrada[3], Entrada[2], Entrada[1]);
  and and_5 (and_5_out, Entrada[3], Entrada[1], Entrada[0]);
  and and_6 (and_6_out, Entrada[3], ~Entrada[2], ~Entrada[1]);  // AND_Gate
  or or_1 (out_2, and_1_out, and_2_out, and_3_out, and_4_out, and_5_out, and_6_out);
endmodule

module Logica_seg_3 (
  input  [3:0] Entrada,
  output out_2
);

  wire and_1_out, and_2_out, and_3_out, and_4_out;

  and and_1 (and_1_out, ~Entrada[3], ~Entrada[2], ~Entrada[0]);  // AND_Gate
  and and_2 (and_2_out, ~Entrada[3], Entrada[2], Entrada[0]);  // AND_Gate
  and and_3 (and_3_out, Entrada[3], Entrada[1], Entrada[0]);
  and and_4 (and_4_out, Entrada[3], ~Entrada[2]);  // AND_Gate
  or or_1 (out_2, and_1_out, and_2_out, and_3_out, and_4_out);
endmodule

module Logica_seg_4 (
  input  [3:0] Entrada,
  output out_2
);

  wire and_1_out, and_2_out, and_3_out, and_4_out, and_5_out;

  and and_1 (and_1_out, ~Entrada[1], Entrada[0]);  // AND_Gate
  and and_2 (and_2_out, ~Entrada[3], ~Entrada[2], Entrada[1]);  // AND_Gate
  and and_3 (and_3_out, Entrada[3], ~Entrada[2], Entrada[1], ~Entrada[0]);  // AND_Gate
  and and_4 (and_4_out, Entrada[3], Entrada[2], Entrada[1], Entrada[0]);
  and and_5 (and_5_out, Entrada[3], Entrada[2], ~Entrada[1], ~Entrada[0]);  // AND_Gate
  or or_1 (out_2, and_1_out, and_2_out, and_3_out, and_4_out, and_5_out);
endmodule

module Logica_seg_5 (
  input  [3:0] Entrada,
  output out_2
);

  or or_1 (out_2, ~Entrada[3], Entrada[2], ~Entrada[1], Entrada[0]);  // OR_Gate
endmodule

module Logica_seg_6 (
  input  [3:0] Entrada,
  output out_2
);

  or or_1 (out_2, Entrada[2], ~Entrada[2]);  // OR_Gate
endmodule

module Logica_seg_7 (
  input  [3:0] Entrada,
  output out_2
);

  wire and_1_out, and_2_out, and_3_out, and_4_out, and_5_out;

  and and_1 (and_1_out, ~Entrada[1], ~Entrada[0]);  // AND_Gate
  and and_2 (and_2_out, ~Entrada[3], Entrada[2], Entrada[1]);  // AND_Gate
  and and_3 (and_3_out, Entrada[3], Entrada[1], ~Entrada[0]);  // AND_Gate
  and and_4 (and_4_out, ~Entrada[3], ~Entrada[2], Entrada[1], Entrada[0]);  // AND_Gate
  and and_5 (and_5_out, Entrada[3], ~Entrada[2], ~Entrada[1], Entrada[0]);  // AND_Gate
  or or_1 (out_2, and_1_out, and_2_out, and_3_out, and_4_out, and_5_out);
endmodule
