// Logisim project display.circ as structural Verilog: 8 circuits, main circuit main
module main (
  input  in_1,
  input  in_2,
  input  in_3,
  input  in_4,
  output out_5,
  output out_6,
  output out_7,
  output out_8,
  output out_9,
  output out_10,
  output out_11
);

  segmento_a Logica_segmento_a (.in_1({in_1, in_2, in_3, in_4}), .out_2(out_5));
  segmento_b Logica_segmento_b (.in_1({in_1, in_2, in_3, in_4}), .out_2(out_6));
  segmento_c Logica_segmento_c (.in_1({in_1, in_2, in_3, in_4}), .out_2(out_7));
  segmento_d Logica_segmento_d (.in_1({in_1, in_2, in_3, in_4}), .out_2(out_8));
  Segmento_e Logica_segmento_e (.in_1({in_1, in_2, in_3, in_4}), .out_2(out_9));
  Segmento_f Logicasegmento_f (.in_1({in_1, in_2, in_3, in_4}), .out_2(out_10));
  Segmento_g Logica_segmento_g (.in_1({in_1, in_2, in_3, in_4}), .out_2(out_11));
endmodule

module segmento_a (
  input  [3:0] in_1,
  output out_2
);

  wire and_1_out, and_2_out, and_3_out, and_4_out;

  and and_1 (and_1_out, in_1[1], ~in_1[0]);  // AND_Gate
  and and_2 (and_2_out, in_1[3], in_1[2]);
  and and_3 (and_3_out, ~in_1[3], in_1[2], ~in_1[1]);  // AND_Gate
  and and_4 (and_4_out, ~in_1[3], ~in_1[1], ~in_1[0]);  // AND_Gate
  or or_1 (out_2, and_1_out, and_2_out, and_3_out, and_4_out);
endmodule

module segmento_b (
  input  [3:0] in_1,
  output out_2
);

  wire and_1_out, and_2_out, and_3_out, and_4_out;

  and and_1 (and_1_out, ~in_1[2], ~in_1[0], ~in_1[1]);  // AND_Gate
  and and_2 (and_2_out, in_1[3], ~in_1[2], ~in_1[1]);  // AND_Gate
  and and_3 (and_3_out, ~in_1[3], in_1[1], in_1[0]);  // AND_Gate
  and and_4 (and_4_out, in_1[3], in_1[2], in_1[1]);
  or or_1 (out_2, and_1_out, and_2_out, and_3_out, and_4_out);
endmodule

module segmento_c (
  input  [3:0] in_1,
  output out_2
);

  wire and_1_out, and_2_out, and_3_out, and_4_out, and_5_out;

  and and_1 (and_1_out, ~in_1[3], ~in_1[2], ~in_1[1]);  // AND_Gate
  and and_2 (and_2_out, ~in_1[3], in_1[1], in_1[0]);  // AND_Gate
  and and_3 (and_3_out, ~in_1[3], in_1[2], in_1[1]);  // AND_Gate
  and and_4 (and_4_out, in_1[3], in_1[1], ~in_1[0]);  // AND_Gate
  and and_5 (and_5_out, in_1[3], ~in_1[1]);  // AND_Gate
  or or_1 (out_2, and_1_out, and_2_out, and_3_out, and_4_out, and_5_out);
endmodule

module segmento_d (
  input  [3:0] in_1,
  output out_2
);

  wire and_1_out, and_2_out, and_3_out, and_4_out;

  and and_1 (and_1_out, ~in_1[3], in_1[1], ~in_1[0]);  // AND_Gate
  and and_2 (and_2_out, in_1[2], in_1[1], ~in_1[0]);  // AND_Gate
  and and_3 (and_3_out, ~in_1[3], in_1[2], ~in_1[0]);  // AND_Gate
  and and_4 (and_4_out, ~in_1[2], in_1[0]);  // AND_Gate
  or or_1 (out_2, and_1_out, and_2_out, and_3_out, and_4_out);
endmodule

module Segmento_e (
  input  [3:0] in_1,
  output out_2
);

  wire and_1_out, and_2_out, and_3_out, not_1_out;

  and and_1 (and_1_out, in_1[3], in_1[0]);
  and and_2 (and_2_out, in_1[3], in_1[1]);
  and and_3 (and_3_out, in_1[3], in_1[2]);
  not not_1 (not_1_out, in_1[3]);
  or or_1 (out_2, and_1_out, and_2_out, and_3_out, not_1_out);
endmodule

module Segmento_f (
  input  [3:0] in_1,
  output out_2
);

  wire and_1_out, and_2_out, and_3_out, and_4_out;

  and and_1 (and_1_out, ~in_1[3], ~in_1[1]);  // AND_Gate
  and and_2 (and_2_out, ~in_1[3], in_1[2]);  // AND_Gate
  and and_3 (and_3_out, in_1[1], ~in_1[0]);  // AND_Gate
  and and_4 (and_4_out, in_1[3], in_1[1]);
  or or_1 (out_2, and_1_out, and_2_out, and_3_out, and_4_out);
endmodule

module Segmento_g (
  input  [3:0] in_1,
  output out_2
);

  wire and_1_out, and_2_out, and_3_out, and_4_out, and_5_out;

  and and_1 (and_1_out, ~in_1[3], ~in_1[1]);  // AND_Gate
  and and_2 (and_2_out, ~in_1[3], in_1[0]);  // AND_Gate
  and and_3 (and_3_out, in_1[2], ~in_1[1], ~in_1[0]);  // AND_Gate
  and and_4 (and_4_out, in_1[2], in_1[1], in_1[0]);
  and and_5 (and_5_out, in_1[3], ~in_1[2], in_1[1], ~in_1[0]);  // AND_Gate
  or or_1 (out_2, and_1_out, and_2_out, and_3_out, and_4_out, and_5_out);
endmodule
