// Logisim project mapa.circ as structural Verilog: 12 circuits, main circuit main
module Logica_seg_1 (
  input  [3:0] Entrada,
  output out_2
);

  wire and_1_out, and_2_out, and_3_out, and_4_out, and_5_out;

  and and_1 (and_1_out, Entrada[3], ~Entrada[1]);  // AND_Gate
  and and_2 (and_2_out, Entrada[1], ~Entrada[0]);  // AND_Gate
  and and_3 (and_3_out, Entrada[3], Entrada[2]);
  and and_4 (and_4_out, Entrada[2], ~Entrada[1], ~Entrada[0]);  // AND_Gate
  and and_5 (and_5_out, ~Entrada[3], ~Entrada[2], Entrada[1]);  // AND_Gate
  or or_1 (out_2, and_1_out, and_2_out, and_3_out, and_4_out, and_5_out);
endmodule

module Logica_seg_2 (
  input  [3:0] Entrada,
  output out_2
);

  wire and_1_out, and_2_out, and_3_out, and_4_out, and_5_out, and_6_out;

  and and_1 (and_1_out, ~Entrada[3], ~Entrada[2], ~Entrada[0]);  // AND_Gate
  and and_2 (and_2_out, ~Entrada[3], Entrada[2], ~Entrada[1]);  // AND_Gate
  and and_3 (and_3_out, Entrada[2], Entrada[1], Entrada[0]);
  and and_4 (and_4_out, Entrada[3], Entrada[2], Entrada[1]);
  and and_5 (and_5_out, Entrada[3], Entrada[1], Entrada[0]);
  and and_6 (and_6_out, Entrada[3], ~Entrada[2], ~Entrada[1]);  // AND_Gate
  or or_1 (out_2, and_1_out, and_2_out, and_3_out, and_4_out, and_5_out, and_6_out);
endmodule

module Logica_seg_3 (
  input  [3:0] Entrada,
  output out_2
);

  wire and_1_out, and_2_out, and_3_out, and_4_out;

  and and_1 (and_1_out, ~Entrada[3], ~Entrada[2], ~Entrada[0]);  // AND_Gate
  and and_2 (and_2_out, ~Entrada[3], Entrada[2], Entrada[0]);  // AND_Gate
  and and_3 (and_3_out, Entrada[3], Entrada[1], Entrada[0]);
  and and_4 (and_4_out, Entrada[3], ~Entrada[2]);  // AND_Gate
  or or_1 (out_2, and_1_out, and_2_out, and_3_out, and_4_out);
endmodule

module Logica_seg_4 (
  input  [3:0] Entrada,
  output out_2
);

  wire and_1_out, and_2_out, and_3_out, and_4_out, and_5_out;

  and and_1 (and_1_out, ~Entrada[1], Entrada[0]);  // AND_Gate
  and and_2 (and_2_out, ~Entrada[3], ~Entrada[2], Entrada[1]);  // AND_Gate
  and and_3 (and_3_out, Entrada[3], ~Entrada[2], Entrada[1], ~Entrada[0]);  // AND_Gate
  and and_4 (and_4_out, Entrada[3], Entrada[2], Entrada[1], Entrada[0]);
  and and_5 (and_5_out, Entrada[3], Entrada[2], ~Entrada[1], ~Entrada[0]);  // AND_Gate
  or or_1 (out_2, and_1_out, and_2_out, and_3_out, and_4_out, and_5_out);
endmodule

module Logica_seg_5 (
  input  [3:0] Entrada,
  output out_2
);

  or or_1 (out_2, ~Entrada[3], Entrada[2], ~Entrada[1], Entrada[0]);  // OR_Gate
endmodule

module Logica_seg_6 (
  input  [3:0] Entrada,
  output out_2
);

  or or_1 (out_2, Entrada[2], ~Entrada[2]);  // OR_Gate
endmodule

module Logica_seg_7 (
  input  [3:0] Entrada,
  output out_2
);

  wire and_1_out, and_2_out, and_3_out, and_4_out, and_5_out;

  and and_1 (and_1_out, ~Entrada[1], ~Entrada[0]);  // AND_Gate
  and and_2 (and_2_out, ~Entrada[3], Entrada[2], Entrada[1]);  // AND_Gate
  and and_3 (and_3_out, Entrada[3], Entrada[1], ~Entrada[0]);  // AND_Gate
  and and_4 (and_4_out, ~Entrada[3], ~Entrada[2], Entrada[1], Entrada[0]);  // AND_Gate
  and and_5 (and_5_out, Entrada[3], ~Entrada[2], ~Entrada[1], Entrada[0]);  // AND_Gate
  or or_1 (out_2, and_1_out, and_2_out, and_3_out, and_4_out, and_5_out);
endmodule

module main (
  input  in_1,
  input  in_2,
  input  in_3,
  input  in_4
);

  wire and_1_out, clock_1_out, d_ff_1_q, d_ff_2_q, d_ff_3_q, d_ff_4_q, d_ff_5_q, d_ff_6_q, d_ff_7_q,
       d_ff_8_q, Logica_bit_a_out_5, Logica_bit_b_out_5, Logica_bit_c_out_5, Logica_bit_d_out_5,
       main_1_out_5, main_1_out_6, main_1_out_7, main_1_out_8, main_1_out_9, main_1_out_10, main_1_out_11,
       multiplexer_1_out, multiplexer_2_out, multiplexer_3_out, multiplexer_4_out, not_1_out, or_1_out,
       xor_1_out, xor_2_out, xor_3_out, xor_4_out;

  Clock clock_1 (.out(clock_1_out));
  D_Flip_Flop d_ff_1 (.clk(clock_1_out), .D(in_1), .Q(d_ff_1_q));  // open: Qn, preset, en, reset
  D_Flip_Flop d_ff_2 (.clk(clock_1_out), .D(in_2), .Q(d_ff_2_q));  // open: Qn, preset, en, reset
  D_Flip_Flop d_ff_3 (.clk(clock_1_out), .D(in_3), .Q(d_ff_3_q));  // open: Qn, preset, en, reset
  D_Flip_Flop d_ff_4 (.clk(clock_1_out), .D(in_4), .Q(d_ff_4_q));  // open: Qn, preset, en, reset
  xor xor_1 (xor_1_out, d_ff_1_q, in_1);
  xor xor_2 (xor_2_out, d_ff_2_q, in_2);
  xor xor_3 (xor_3_out, d_ff_3_q, in_3);
  xor xor_4 (xor_4_out, d_ff_4_q, in_4);
  and and_1 (and_1_out, clock_1_out, not_1_out);
  or or_1 (or_1_out, xor_1_out, xor_2_out, xor_3_out, xor_4_out);
  not not_1 (not_1_out, or_1_out);
  Multiplexer #(.enable("false")) multiplexer_1 (
    .in0(in_4), .in1(Logica_bit_d_out_5), .out(multiplexer_1_out), .sel(not_1_out));
  Multiplexer #(.enable("false")) multiplexer_2 (
    .in0(in_1), .in1(Logica_bit_a_out_5), .out(multiplexer_2_out), .sel(not_1_out));
  Multiplexer #(.enable("false")) multiplexer_3 (
    .in0(in_2), .in1(Logica_bit_b_out_5), .out(multiplexer_3_out), .sel(not_1_out));
  Multiplexer #(.enable("false")) multiplexer_4 (
    .in0(in_3), .in1(Logica_bit_c_out_5), .out(multiplexer_4_out), .sel(not_1_out));
  D_Flip_Flop d_ff_5 (.clk(and_1_out), .D(multiplexer_2_out), .Q(d_ff_5_q));  // open: Qn, preset, en, reset
  D_Flip_Flop d_ff_6 (.clk(and_1_out), .D(multiplexer_3_out), .Q(d_ff_6_q));  // open: Qn, preset, en, reset
  D_Flip_Flop d_ff_7 (.clk(and_1_out), .D(multiplexer_4_out), .Q(d_ff_7_q));  // open: Qn, preset, en, reset
  D_Flip_Flop d_ff_8 (.clk(and_1_out), .D(multiplexer_1_out), .Q(d_ff_8_q));  // open: Qn, preset, en, reset
  logica_bit_a_seq Logica_bit_a (
    .in_1(d_ff_5_q), .in_2(d_ff_6_q), .in_3(d_ff_7_q), .in_4(d_ff_8_q), .out_5(Logica_bit_a_out_5));
  logica_bit_b_seq Logica_bit_b (
    .in_1(d_ff_5_q), .in_2(d_ff_6_q), .in_3(d_ff_7_q), .in_4(d_ff_8_q), .out_5(Logica_bit_b_out_5));
  logica_bit_c_seq Logica_bit_c (
    .in_1(d_ff_5_q), .in_2(d_ff_6_q), .in_3(d_ff_7_q), .in_4(d_ff_8_q), .out_5(Logica_bit_c_out_5));
  logica_bit_d_seq Logica_bit_d (
    .in_1(d_ff_5_q), .in_2(d_ff_6_q), .in_3(d_ff_7_q), .in_4(d_ff_8_q), .out_5(Logica_bit_d_out_5));
  display_main main_1 (
    .in_1(d_ff_5_q), .in_2(d_ff_6_q), .in_3(d_ff_7_q), .in_4(d_ff_8_q), .out_5(main_1_out_5),
    .out_6(main_1_out_6), .out_7(main_1_out_7), .out_8(main_1_out_8), .out_9(main_1_out_9),
    .out_10(main_1_out_10), .out_11(main_1_out_11));
  _7_Segment_Display u_7_segment_display_1 (
    .g(main_1_out_11), .f(main_1_out_10), .a(main_1_out_5), .b(main_1_out_6), .e(main_1_out_9),
    .d(main_1_out_8), .c(main_1_out_7));  // open: dp
endmodule

module logica_bit_a_seq (
  input  in_1,
  input  in_2,
  input  in_3,
  input  in_4,
  output out_5
);

  wire and_1_out, and_2_out, and_3_out;

  and and_1 (and_1_out, in_1, ~in_2);  // AND_Gate
  and and_2 (and_2_out, in_1, in_2, ~in_3);  // AND_Gate
  and and_3 (and_3_out, ~in_1, in_3, in_4);  // AND_Gate
  or or_1 (out_5, and_1_out, and_2_out, and_3_out);
endmodule

module logica_bit_b_seq (
  input  in_1,
  input  in_2,
  input  in_3,
  input  in_4,
  output out_5
);

  wire and_1_out, and_2_out, and_3_out, and_4_out, and_5_out;

  and and_1 (and_1_out, in_1, in_2);
  and and_2 (and_2_out, in_2, in_4);
  and and_3 (and_3_out, in_2, in_3);
  and and_4 (and_4_out, in_1, in_4);
  and and_5 (and_5_out, in_1, in_3);
  or or_1 (out_5, and_1_out, and_2_out, and_3_out, and_4_out, and_5_out);
endmodule

module logica_bit_c_seq (
  input  in_1,
  input  in_2,
  input  in_3,
  input  in_4,
  output out_5
);

  wire and_1_out, and_2_out, and_3_out, and_4_out;

  and and_1 (and_1_out, in_1, in_2, ~in_3);  // AND_Gate
  and and_2 (and_2_out, ~in_1, ~in_2, ~in_3, in_4);  // AND_Gate
  and and_3 (and_3_out, ~in_1, in_2, in_3, ~in_4);  // AND_Gate
  and and_4 (and_4_out, in_2, ~in_3, ~in_4);  // AND_Gate
  or or_1 (out_5, and_1_out, and_2_out, and_3_out, and_4_out);
endmodule

module logica_bit_d_seq (
  input  in_1,
  input  in_2,
  input  in_3,
  input  in_4,
  output out_5
);

  wire and_1_out, and_2_out, and_3_out, and_4_out, and_5_out;

  and and_1 (and_1_out, ~in_1, ~in_3);  // AND_Gate
  and and_2 (and_2_out, in_2, ~in_3, in_4);  // AND_Gate
  and and_3 (and_3_out, in_3, ~in_4);  // AND_Gate
  and and_4 (and_4_out, in_1, in_3);
  and and_5 (and_5_out, in_1, ~in_2, ~in_4);  // AND_Gate
  or or_1 (out_5, and_1_out, and_2_out, and_3_out, and_4_out, and_5_out);
endmodule
